# Fritzing sketch Circuit_diagram (saved by Fritzing 0.9.3b)
breadboards: 1

parts:
  J1 = Basic Force Sensing Resistor (FSR) [package=THT]
  Nano1 = Arduino Nano v2.3
  Part1 = Breakout Board for Electret Microphone
  R1 = Resistor [tolerance=±5% resistance=220 package="1206 [SMD]"]

nets:
  +5V: J1.pin_0, Nano1.+5V, Part1.VCC
  N1: J1.pin_1, Nano1.A0, R1.Pin_0
  GND: Nano1.GND, Part1.GND, R1.Pin_1
  N2: Nano1.D7, Part1.AUD

notes:
  Collision Sensor
  FSR(Force Sensitive Resistor)
  Arduino Nano
  Force Sensitive Resistor :
  Pin1 -> Resistor -> Gnd pin
  Pin1 -> A0 pin
  Pin2 -> +5V pin
  Collision Sensor:
  Vcc -> +5V Pin
  Gnd -> Gnd Pin
  Out -> D7 Pin
